# Fritzing sketch a (saved by Fritzing 0.9.3b)
breadboards: 1

parts:
  Часть1 = Arduino Mega ADK (Rev3)
  U1 = LIPO-1000mAh [package=lipo-1000]
  J1 = Basic Servo
  J2 = Basic Servo
  J3 = Basic Servo
  J4 = Basic Servo
  J5 = Basic Servo
  J6 = Basic Servo
  Q1 = MOSFET-NCHANNEL [package=to220v]
  R1 = Resistor [tolerance=±5% resistance=10k package="0603 [SMD]"]
  R2 = Resistor [tolerance=±5% resistance=220 package="0603 [SMD]"]
  Q2 = MOSFET-NCHANNEL [package=to220v]
  R3 = Resistor [tolerance=±5% resistance=10k package="0603 [SMD]"]
  R4 = Resistor [tolerance=±5% resistance=220 package="0603 [SMD]"]
  RHT1 = Humidity and Temperature Sensor RHT03
  Q3 = MOSFET-NCHANNEL [package=to220v]
  R5 = Resistor [tolerance=±5% resistance=10k package="0603 [SMD]"]
  R6 = Resistor [tolerance=±5% resistance=220 package="0603 [SMD]"]  # not connected
  Часть2 = MicroSD Card Module
  Часть3 = Real Time Clock Module - DS1307 RTC Breakout Board
  Q4 = MOSFET-NCHANNEL [package=to220v]
  R7 = Resistor [tolerance=±5% resistance=10k package="0603 [SMD]"]
  R8 = Resistor [tolerance=±5% resistance=220 package="0603 [SMD]"]
  U2 = ESP8266 WiFi Module

nets:
  N1: Часть1.A0, U2.TXD
  N2: Часть1.A1, U2.RXD
  N3: Часть1.A2, R4.Pin_1
  N4: Часть1.A3, RHT1.Data-signal
  N5: Часть1.D21/SCL, Часть3.SCL
  N6: Часть1.D20/SDA, Часть3.SDA
  N7: Часть1.GND, U1.-
  N8: Часть1.D13_PWM, R2.Pin_1
  N9: Часть1.D12_PWM, J1.pulse
  N10: Часть1.D11_PWM, J2.pulse
  N11: Часть1.D10_PWM, J3.pulse
  N12: Часть1.D9_PWM, J4.pulse
  N13: Часть1.D8_PWM, J5.pulse
  N14: Часть1.IOREF, Часть1.5V, U1.+
  N15: Часть1.D7_PWM, J6.pulse
  N16: Часть1.D28, Часть2.CS
  N17: Часть1.D37, R8.Pin_1
  N18: Часть1.D50/MISO, Часть2.MISO
  N19: Часть1.D51/MOSI, Часть2.MOSI
  N20: Часть1.D52/SCK, Часть2.SCK
  N21: J6.gnd, Q1.G
  N22: Q1.S, R1.Pin_1
  GND: R1.Pin_0, R3.Pin_0, R5.Pin_0, R7.Pin_0
  N23: Q2.G, U2.GND
  N24: Q2.S, R3.Pin_1
  N25: Q3.S, R5.Pin_1
  N26: Часть2.GND, Q4.G
  N27: Q4.S, R7.Pin_1
